# Fritzing sketch Computer Block (saved by Fritzing 0.9.3b)

parts:
  Teensy1 = Teensy 3.6 (Basic)
  Parça1 = u-blox NEO-6M GPS Breakout
  Parça2 = NRF24L01+ Breakout Board
  C1 = Capacitor Polarized [package=cpol-radial-100uf-25v]
  M1 = gy9250
  Serial_IO1 = female pin header, 10 pins [form="♀ (female)"]
  Serial_IO2 = female pin header, 10 pins [form="♀ (female)"]
  Serial_IO3 = female pin header, 3 pins [form="♀ (female)"]
  Serial_IO4 = female pin header, 3 pins [form="♀ (female)"]

nets:
  GND: Teensy1.GND, Teensy1.GND1, Parça1.GND, Parça2.GND, C1.-, M1.pin2, Serial_IO2.pin1
  N1: Teensy1.D0, Parça1.TXD
  N2: Teensy1.D1, Parça1.RXD
  N3: Teensy1.D4, Serial_IO2.pin8
  N4: Teensy1.D5, Serial_IO1.pin8
  N5: Teensy1.D6, Serial_IO2.pin9
  N6: Teensy1.D7, Parça2.CE
  N7: Teensy1.D8, Parça2.CS
  N8: Teensy1.D11, Parça2.MOSI
  N9: Teensy1.D12, Parça2.MISO
  N10: Teensy1.D13, Parça2.SCK
  N11: Teensy1.A0/D14, Serial_IO1.pin6
  N12: Teensy1.A1/D15, Serial_IO2.pin6
  N13: Teensy1.A2/D16, Serial_IO1.pin5
  N14: Teensy1.A3/D17, Serial_IO2.pin5
  VCC: Teensy1.3V3, Teensy1.3V3_1, Parça1.VCC, Parça2.VCC, C1.+, M1.pin1, Serial_IO1.pin1
  N15: Teensy1.D24, Serial_IO1.pin9
  N16: Teensy1.D25, Serial_IO2.pin10
  N17: Teensy1.D26, Serial_IO1.pin10
  N18: Teensy1.D27, Serial_IO3.pin1
  N19: Teensy1.D28, Serial_IO4.pin1
  N20: Teensy1.D29, Serial_IO3.pin2
  N21: Teensy1.D30, Serial_IO4.pin2
  N22: Teensy1.D31, Serial_IO3.pin3
  N23: Teensy1.D32, Serial_IO4.pin3
  N24: Teensy1.D33, M1.pin3
  N25: Teensy1.D34, M1.pin4
  N26: Teensy1.D37, Serial_IO1.pin7
  N27: Teensy1.D38, Serial_IO2.pin7

custom parts:
  Teensy 3.6 (Basic): The Teensy is a complete USB-based microcontoller development system, in a very small footprint, capable of implementing many types of projects. All programming is done via the USB port. No special programmer is needed, only a standard micro-USB cable and a PC or Macintosh with a USB port.
  gy9250: MPU-9250 module (three-axis gyroscope + three-axis acceleration + three-axis magnetic field). The generic model from ebay et. al. rather than the Sparkfun version.
