# Fritzing sketch Controller (saved by Fritzing 0.9.3b)

parts:
  Parça2 = NRF24L01+ Breakout Board
  RE1 = Rotary Encoder [package=THT]
  S2 = Toggle Switch [package=THT]
  S3 = Toggle Switch [package=THT]
  S4 = Toggle Switch [package=THT]
  S5 = Toggle Switch [package=THT]
  S7 = Pushbutton [package="[THT]"]
  R1 = Resistor [tolerance=±5% resistance=1k package=THT]
  S8 = Pushbutton [package="[THT]"]
  R2 = Resistor [tolerance=±5% resistance=1k package=THT]
  S10 = Pushbutton [package="[THT]"]
  R4 = Resistor [tolerance=±5% resistance=1k package=THT]
  RE2 = Rotary Encoder [package=THT]
  RE3 = Rotary Encoder [package=THT]
  RE4 = Rotary Encoder [package=THT]
  RE5 = Rotary Encoder [package=THT]
  RE6 = Rotary Encoder [package=THT]
  LCD1 = LCD screen
  Parça3 = Arduino Micro (Rev3)
  R6 = Resistor [tolerance=±5% resistance=220 package=THT]
  R7 = Resistor [tolerance=±5% resistance=1k package=THT]
  R10 = Resistor [tolerance=±5% resistance=1k package=THT]

nets:
  GND: Parça2.GND, R1.Pin_0, R2.Pin_0, R4.Pin_0, RE4.EncoderPinA, RE5.EncoderPinA, RE6.EncoderPinA, Parça3.GND, R10.Pin_1
  VCC: Parça2.VCC, RE1.EncoderPinB, RE2.EncoderPinB, RE3.EncoderPinB, RE4.EncoderPinB, RE5.EncoderPinB, RE6.EncoderPinB, Parça3.3V3
  N1: Parça2.CE, Parça3.D6_PWM/A7
  N2: Parça2.CS, Parça3.D7
  N3: Parça2.SCK, Parça3.SCK
  N4: Parça2.MOSI, Parça3.MOSI
  N5: Parça2.MISO, Parça3.MISO
  N6: RE1.EncoderPinA, RE2.EncoderPinA, RE3.EncoderPinA, LCD1.VSS, LCD1.R/W, R6.Pin_0, R7.Pin_0
  N7: RE1.EncoderPinC, Parça3.A0
  N8: S2.COM, S7.Pin_3, S7.Pin_4, R1.Pin_1, Parça3.D12_PWM/A11
  N9: S2.L2, S3.L2, S4.L2, S5.L2, Parça3.D8_PWM/A8
  N10: S3.COM, Parça3.D9_PWM/A9, R10.Pin_0
  N11: S4.COM, S10.Pin_3, S10.Pin_4, R4.Pin_1, Parça3.D10_PWM/A10
  N12: S5.COM, S8.Pin_4, R2.Pin_1, Parça3.D11_PWM
  N13: S7.Pin_2, S8.Pin_2, S10.Pin_2, Parça3.D5_PWM
  N14: RE2.EncoderPinC, Parça3.A1
  N15: RE3.EncoderPinC, Parça3.A2
  N16: RE4.EncoderPinC, Parça3.A5
  N17: RE5.EncoderPinC, Parça3.A3
  N18: RE6.EncoderPinC, Parça3.A4
  VDD: LCD1.VDD, LCD1.LED+, Parça3.5V
  N19: LCD1.V0, R7.Pin_1
  N20: LCD1.RS, Parça3.D13_PWM
  N21: LCD1.E, Parça3.D4_PWM/A6
  N22: LCD1.DB4, Parça3.D3/SCL
  N23: LCD1.DB5, Parça3.D2/SDA
  N24: LCD1.DB6, Parça3.D0/RX
  N25: LCD1.DB7, Parça3.D1/TX
  N26: LCD1.LED-, R6.Pin_1
