# Fritzing sketch Drone Case1 (saved by Fritzing 0.9.3b)

parts:
  J1 = female pin header, 2 pins [form="♀ (female)"]
  J2 = female pin header, 2 pins [form="♀ (female)"]
  M1 = DC Motor
  Parça1 = Arduino Pro Mini V2 (5V)
  D2F1 = D2F-FL Omron Snap Action Limit Switch with Level
  Q2 = NPN-Transistor [package="TO92 [THT]"]
  R3 = Resistor [tolerance=±5% resistance=1k package=THT]
  Q3 = NPN-Transistor [package="TO92 [THT]"]
  R4 = Resistor [tolerance=±5% resistance=1k package=THT]
  Q4 = NPN-Transistor [package="TO92 [THT]"]
  Q5 = NPN-Transistor [package="TO92 [THT]"]
  R5 = Resistor [tolerance=±5% resistance=1k package=THT]
  R6 = Resistor [tolerance=±5% resistance=1k package=THT]
  Q6 = NPN-Transistor [package="TO92 [THT]"]
  Q7 = NPN-Transistor [package="TO92 [THT]"]
  R7 = Resistor [tolerance=±5% resistance=1k package=THT]
  R8 = Resistor [tolerance=±5% resistance=1k package=THT]
  R9 = Resistor [tolerance=±5% resistance=10k package=THT]
  R10 = Resistor [tolerance=±5% resistance=10k package=THT]
  Q8 = NPN-Transistor [package="TO92 [THT]"]
  Q9 = NPN-Transistor [package="TO92 [THT]"]
  R11 = Resistor [tolerance=±5% resistance=1k package=THT]
  R12 = Resistor [tolerance=±5% resistance=10k package=THT]
  R13 = Resistor [tolerance=±5% resistance=1k package=THT]
  R14 = Resistor [tolerance=±5% resistance=10k package=THT]

nets:
  N1: J1.pin1, Parça1.A5
  N2: J1.pin2, Parça1.A4
  N3: J2.pin1, Parça1.RAW, Q3.C, Q4.C, R9.Pin_0, R14.Pin_0
  N4: J2.pin2, Parça1.GND, Q2.E, Q5.E, Q6.E, Q7.E, Q8.E, Q9.E
  N5: M1.pin_1, Q4.E, Q5.C
  N6: M1.pin_2, Q2.C, Q3.E
  N7: Parça1.VCC, D2F1.NO, R10.Pin_0, R12.Pin_0
  N8: Parça1.SCK, D2F1.COM
  N9: Parça1.MISO, R7.Pin_0
  N10: Parça1.MOSI, R13.Pin_0
  N11: Q2.B, R3.Pin_0
  N12: R3.Pin_1, R5.Pin_0, Q8.C, R14.Pin_1
  N13: Q3.B, R4.Pin_0
  N14: R4.Pin_1, R6.Pin_1, Q7.C, R9.Pin_1
  N15: Q4.B, R5.Pin_1
  N16: Q5.B, R6.Pin_0
  N17: Q6.B, R7.Pin_1
  N18: Q6.C, R8.Pin_1, R10.Pin_1
  N19: Q7.B, R8.Pin_0
  N20: Q8.B, R11.Pin_0
  N21: Q9.B, R13.Pin_1
  N22: Q9.C, R11.Pin_1, R12.Pin_1

notes:
  1K
  10K

custom parts:
  Arduino Pro Mini V2 (5V): Arduino Pro Mini V2 There are several different layouts for this board out there. This one is modeled after the Sparkfun 11113 board but a few of the pins have been moved around.
  D2F-FL Omron Snap Action Limit Switch with Level: Snap action switch with stainless steel lever.
