# Fritzing sketch LOTP_Gas_Module (saved by Fritzing 0.9.3b)

parts:
  Parça1 = MQ-7 breakout
  Parça2 = Arduino Pro Mini V2 (5V)
  LED1 = LED - 5mm [color="Red (633nm)" package="5 mm [THT]"]
  LED2 = LED - 5mm [color="Green (555nm)" package="5 mm [THT]"]
  J1 = Piezo Speaker
  J2 = female pin header, 2 pins [form="♀ (female)"]
  J3 = female pin header, 2 pins [form="♀ (female)"]

nets:
  N1: Parça1.VCC, Parça2.RAW, J3.pin1
  GND: Parça1.GND, Parça2.GND, LED1.cathode, LED2.cathode, J1.pin1, J3.pin2
  N2: Parça1.AO, Parça2.A0
  N3: Parça2.A4, J2.pin1
  N4: Parça2.A5, J2.pin2
  N5: Parça2.MISO, J1.pin2
  N6: Parça2.MOSI, LED2.anode
  N7: Parça2.D10, LED1.anode

custom parts:
  MQ-7 breakout: SKU: 101282
  Arduino Pro Mini V2 (5V): Arduino Pro Mini V2 There are several different layouts for this board out there. This one is modeled after the Sparkfun 11113 board but a few of the pins have been moved around.
