# Fritzing sketch Lidar (saved by Fritzing 0.9.3b)

parts:
  Parça2 = GY-VL53L0XV2 Laser Ranger Module
  J1 = female pin header, 2 pins [form="♀ (female)"]
  J2 = female pin header, 2 pins [form="♀ (female)"]
  R2 = Resistor [tolerance=±5% resistance=1k package=THT]
  Q1 = NPN-Transistor [package="TO92 [THT]"]
  D1 = Rectifier Diode [part_number=1N4001 package="300 mil [THT]"]
  C1 = Ceramic Capacitor [capacitance=100nF package="100 mil [THT, multilayer]"]
  J4 = female pin header, 4 pins [form="♀ (female)"]
  J5 = female pin header, 4 pins [form="♀ (female)"]
  J7 = female pin header, 1 pin [form="♀ (female)"]
  R3 = Resistor [tolerance=±5% resistance=10k package=THT]
  J8 = female pin header, 1 pin [form="♀ (female)"]
  M1 = DC Motor
  Parça1 = Arduino Pro Mini V2 (5V)

nets:
  N1: Parça2.VCC, J5.pin1, J8.pin1
  N2: Parça2.GND, J5.pin2
  N3: Parça2.SCL, J5.pin3
  N4: Parça2.SDA, J5.pin4
  N5: J1.pin1, J4.pin3, Parça1.A5
  N6: J1.pin2, J4.pin4, Parça1.A4
  N7: J2.pin1, D1.cathode, C1.0, M1.pin_1, Parça1.RAW
  N8: J2.pin2, Q1.E
  N9: R2.Pin_0, Q1.B
  N10: R2.Pin_1, Parça1.SCK
  N11: Q1.C, D1.anode, C1.1, M1.pin_2
  N12: J4.pin1, Parça1.VCC
  N13: J4.pin2, R3.Pin_0, Parça1.GND
  N14: J7.pin1, R3.Pin_1, Parça1.MISO

custom parts:
  GY-VL53L0XV2 Laser Ranger Module: The GY-VL53L0XV2 is based on the VL53L0X from ST Microelectronics, a time-of-flight ranging system integrated into a compact module.
  Arduino Pro Mini V2 (5V): Arduino Pro Mini V2 There are several different layouts for this board out there. This one is modeled after the Sparkfun 11113 board but a few of the pins have been moved around.
