# Fritzing sketch Main Distrubute Board (saved by Fritzing 0.9.3b)

parts:
  J1 = Basic Force Sensing Resistor (FSR) [package=THT]
  J2 = Basic Force Sensing Resistor (FSR) [package=THT]
  J3 = Basic Force Sensing Resistor (FSR) [package=THT]
  J4 = Basic Force Sensing Resistor (FSR) [package=THT]
  Force_Sensors1 = female pin header, 4 pins [form="♀ (female)"]
  R1 = Resistor [tolerance=±5% resistance=10k package=THT]
  R2 = Resistor [tolerance=±5% resistance=10k package=THT]
  R3 = Resistor [tolerance=±5% resistance=10k package=THT]
  R4 = Resistor [tolerance=±5% resistance=10k package=THT]
  Servos = double row female pin header, 12 pins [form="♀ (female)"]
  Servo1 = female pin header, 3 pins [form="♀ (female)"]
  Servo2 = female pin header, 3 pins [form="♀ (female)"]
  Servo3 = female pin header, 3 pins [form="♀ (female)"]
  Servo4 = female pin header, 3 pins [form="♀ (female)"]
  Servo5 = female pin header, 3 pins [form="♀ (female)"]
  Servo6 = female pin header, 3 pins [form="♀ (female)"]
  Servo7 = female pin header, 3 pins [form="♀ (female)"]
  Servo8 = female pin header, 3 pins [form="♀ (female)"]
  Servo9 = female pin header, 3 pins [form="♀ (female)"]
  Servo10 = female pin header, 3 pins [form="♀ (female)"]
  Servo11 = female pin header, 3 pins [form="♀ (female)"]
  Servo12 = female pin header, 3 pins [form="♀ (female)"]
  Power_7~6V = female pin header, 2 pins [form="♀ (female)"]
  Power_5V = female pin header, 2 pins [form="♀ (female)"]
  Power_3_3V = female pin header, 2 pins [form="♀ (female)"]
  Power6 = female pin header, 2 pins [form="♀ (female)"]
  Power7 = female pin header, 2 pins [form="♀ (female)"]
  Serial_IO1 = double row female pin header, 2 pins [form="♀ (female)"]
  Serial_IO2 = double row female pin header, 2 pins [form="♀ (female)"]
  Power_5V1 = female pin header, 2 pins [form="♀ (female)"]
  Power_3_3V1 = female pin header, 2 pins [form="♀ (female)"]
  Serial_IO = double row female pin header, 2 pins [form="♀ (female)"]
  Serial_IO3 = double row female pin header, 2 pins [form="♀ (female)"]
  Serial_IO4 = double row female pin header, 2 pins [form="♀ (female)"]
  Serial_IO5 = double row female pin header, 2 pins [form="♀ (female)"]
  Serial_IO6 = double row female pin header, 2 pins [form="♀ (female)"]
  Power_3_3V2 = female pin header, 2 pins [form="♀ (female)"]
  Power_5V2 = female pin header, 2 pins [form="♀ (female)"]
  Power_3_3V3 = female pin header, 2 pins [form="♀ (female)"]
  Power_5V3 = female pin header, 2 pins [form="♀ (female)"]
  Power_3_3V4 = female pin header, 2 pins [form="♀ (female)"]
  Power_5V4 = female pin header, 2 pins [form="♀ (female)"]
  Power_5V5 = female pin header, 2 pins [form="♀ (female)"]
  Power_5V6 = female pin header, 2 pins [form="♀ (female)"]
  Power_3_3V5 = female pin header, 2 pins [form="♀ (female)"]
  Power_3_3V6 = female pin header, 2 pins [form="♀ (female)"]
  Power8 = female pin header, 2 pins [form="♀ (female)"]
  Power9 = female pin header, 2 pins [form="♀ (female)"]
  Power10 = female pin header, 2 pins [form="♀ (female)"]
  Power11 = female pin header, 2 pins [form="♀ (female)"]
  Power12 = female pin header, 2 pins [form="♀ (female)"]
  Power13 = female pin header, 2 pins [form="♀ (female)"]
  Power_7~6V1 = female pin header, 2 pins [form="♀ (female)"]
  Power_7~6V2 = female pin header, 2 pins [form="♀ (female)"]
  Power_7~6V3 = female pin header, 2 pins [form="♀ (female)"]
  Power1 = single row smd female pin header, 2 pins [form="♀ (female)"]

nets:
  N1: J1.pin_0, J2.pin_0, J3.pin_0, J4.pin_0, Power_3_3V.pin2, Power_3_3V1.pin2, Power_3_3V2.pin2, Power_3_3V3.pin2, Power_3_3V4.pin2, Power_3_3V5.pin2, Power_3_3V6.pin2, Power1.pin2
  N2: J1.pin_1, Force_Sensors1.pin1, R1.Pin_0
  N3: J2.pin_1, Force_Sensors1.pin2, R2.Pin_0
  N4: J3.pin_1, Force_Sensors1.pin4, R3.Pin_0
  N5: J4.pin_1, Force_Sensors1.pin3, R4.Pin_0
  N6: R1.Pin_1, R2.Pin_1, R3.Pin_1, R4.Pin_1, Power_3_3V.pin1, Power_3_3V1.pin1, Power_3_3V2.pin1, Power_3_3V3.pin1, Power_3_3V4.pin1, Power_3_3V5.pin1, Power_3_3V6.pin1, Power1.pin1
  N7: Servos.pin1, Servo1.pin3
  N8: Servos.pin2, Servo2.pin3
  N9: Servos.pin3, Servo3.pin3
  N10: Servos.pin4, Servo4.pin3
  N11: Servos.pin5, Servo6.pin3
  N12: Servos.pin6, Servo5.pin3
  N13: Servos.pin7, Servo11.pin3
  N14: Servos.pin8, Servo8.pin3
  N15: Servos.pin9, Servo7.pin3
  N16: Servos.pin10, Servo12.pin3
  N17: Servos.pin11, Servo9.pin3
  N18: Servos.pin12, Servo10.pin3
  N19: Servo1.pin1, Servo2.pin1, Servo3.pin1, Power_7~6V.pin1
  N20: Servo1.pin2, Servo2.pin2, Servo3.pin2, Power_7~6V.pin2
  N21: Servo4.pin1, Servo5.pin1, Servo6.pin1, Power_7~6V1.pin1
  N22: Servo4.pin2, Servo5.pin2, Servo6.pin2, Power_7~6V1.pin2
  N23: Servo7.pin1, Servo8.pin1, Servo11.pin1, Power_7~6V2.pin1
  N24: Servo7.pin2, Servo8.pin2, Servo11.pin2, Power_7~6V2.pin2
  N25: Servo9.pin1, Servo10.pin1, Servo12.pin1, Power_7~6V3.pin1
  N26: Servo9.pin2, Servo10.pin2, Servo12.pin2, Power_7~6V3.pin2
  N27: Power_5V.pin1, Power_5V1.pin1, Power_5V2.pin1, Power_5V3.pin1, Power_5V4.pin1, Power_5V5.pin1, Power_5V6.pin1
  N28: Power_5V.pin2, Power_5V1.pin2, Power_5V2.pin2, Power_5V3.pin2, Power_5V4.pin2, Power_5V5.pin2, Power_5V6.pin2
  N29: Power6.pin1, Power7.pin1, Power8.pin1, Power9.pin1, Power10.pin1, Power11.pin1, Power12.pin1, Power13.pin1
  N30: Power6.pin2, Power7.pin2, Power8.pin2, Power9.pin2, Power10.pin2, Power11.pin2, Power12.pin2, Power13.pin2
  N31: Serial_IO1.pin1, Serial_IO2.pin1, Serial_IO.pin1, Serial_IO3.pin1, Serial_IO4.pin1, Serial_IO5.pin1, Serial_IO6.pin1
  N32: Serial_IO1.pin2, Serial_IO2.pin2, Serial_IO.pin2, Serial_IO3.pin2, Serial_IO4.pin2, Serial_IO5.pin2, Serial_IO6.pin2
