# Fritzing sketch Regulator Mobule (saved by Fritzing 0.9.3b)

parts:
  M1 = RioRand LM2596
  M2 = RioRand LM2596
  M3 = RioRand LM2596
  M4 = RioRand LM2596
  M5 = RioRand LM2596
  M6 = RioRand LM2596
  Servos1 = female pin header, 7 pins [form="♀ (female)"]
  Servos2 = female pin header, 7 pins [form="♀ (female)"]

nets:
  N1: M1.Pin_1, M2.Pin_1, M3.Pin_1, M4.Pin_1, M5.Pin_1, M6.Pin_1, Servos2.pin1
  N2: M1.Pin_2, M2.Pin_2, M3.Pin_2, M4.Pin_2, M5.Pin_2, M6.Pin_2, Servos1.pin1
  N3: M1.Pin_3, Servos2.pin6
  N4: M1.Pin_4, Servos1.pin6
  N5: M2.Pin_3, Servos2.pin7
  N6: M2.Pin_4, Servos1.pin7
  N7: M3.Pin_3, Servos2.pin5
  N8: M3.Pin_4, Servos1.pin5
  N9: M4.Pin_3, Servos2.pin4
  N10: M4.Pin_4, Servos1.pin4
  N11: M5.Pin_3, Servos2.pin3
  N12: M5.Pin_4, Servos1.pin3
  N13: M6.Pin_3, Servos2.pin2
  N14: M6.Pin_4, Servos1.pin2

notes:
  6V
  5V
  3.3V
